# Fritzing sketch circuit-diagram (saved by Fritzing 0.9.3b)

parts:
  Part1 = Arduino Uno (Rev3) - ICSP
  OLED_I2C1 = OLED 128x64 I2C Monochrome Display
  Header1 = 2 pin header [package=THT]
  TRM1 = Terminal 2pin
  TRM2 = Terminal 2pin
  S1 = Pushbutton [package="[THT]"]
  R1 = Resistor [tolerance=±5% resistance=220 package="0402 [SMD]"]
  R2 = Resistor [tolerance=±5% resistance=220 package="0603 [SMD]"]
  R3 = Resistor [tolerance=±5% resistance=220 package="0603 [SMD]"]

nets:
  N1: Part1.A0, Header1.pin_1#1, S1.Pin_3, R2.Pin_0
  N2: Part1.A1, TRM2.pin_1, R1.Pin_1, R3.Pin_0
  N3: Part1.A4/SDA, OLED_I2C1.SDA
  N4: Part1.A5/SCL, OLED_I2C1.SCK
  5V: Part1.5V, OLED_I2C1.VDD, Header1.pin_1#0, S1.Pin_1
  GND: Part1.GND, OLED_I2C1.GND, TRM1.pin_2, TRM2.pin_2, R2.Pin_1, R3.Pin_1
  N5: TRM1.pin_1, R1.Pin_0

notes:
  220Ohm
  10KOhm
  7KOhm

custom parts:
  2 pin header: 2 pin male to male header
  Terminal 2pin: 2-pin Terminal Block
